// Logisim project s-mips.circ as structural Verilog: 18 circuits, main circuit S-MIPS Board
module S_MIPS_Board (
  input  DESHABILITAR_DISPATCHER,
  output halt
);

  wire button_1_out, CLK, CS, d_ff_1_q, LCLR, LoadRAM, LoadRAMOn, LW, R_R_W, R_W, ram_dispatcher_1_finished,
       RCS, Reset_out, RST, TTY_EN;
  wire [2:0] KDB;
  wire [3:0] LMask, Mask, ram_1_read_time, ram_1_write_time, RMask;
  wire [6:0] KDB_DATA, TTY_DATA;
  wire [15:0] Addr, LAddr, RAddr;
  wire [31:0] I0, I1, I2, I3, LData, ram_1_data_out_0, ram_1_data_out_1, ram_1_data_out_2, ram_1_data_out_3,
       RI0, RI1, RI2, RI3;

  TTY #(.rows(25), .cols(80)) tty_1 (.data(TTY_DATA), .clk(CLK), .we(TTY_EN), .clr(RST));
  not not_1 (LoadRAMOn, ram_dispatcher_1_finished);
  RAM_Dispatcher ram_dispatcher_1 (
    .WriteTime(ram_1_write_time), .Clock(CLK), .Data(LData), .Address(LAddr), .Mask(LMask),
    .Finished(ram_dispatcher_1_finished), .Write(LW), .CLR(LCLR));
  Keyboard #(.buflen(64)) keyboard_1 (.clk(CLK), .re(KDB[0]), .avail(KDB[2]), .data(KDB_DATA));  // open: clr
  RAM ram_1 (
    .Address(RAddr), .Data_Out_0(ram_1_data_out_0), .Data_Out_1(ram_1_data_out_1),
    .Data_Out_2(ram_1_data_out_2), .Data_Out_3(ram_1_data_out_3), .Data_In_0(RI0), .Data_In_1(RI1),
    .Data_In_2(RI2), .Data_In_3(RI3), .Mask(RMask), .nRead_Write(R_R_W), .Chip_Select(RCS),
    .Read_Time(ram_1_read_time), .Reset(button_1_out), .Write_Time(ram_1_write_time));
  Button button_1 (.out(button_1_out));
  D_Flip_Flop d_ff_1 (.clk(CLK), .D(1'b1), .Q(d_ff_1_q), .reset(Reset_out));  // open: Qn, preset, en
  Button Reset (.out(Reset_out));
  S_MIPS s_mips_1 (
    .Kbd_Enable(KDB[0]), .Address(Addr), .Kbd_Clear(KDB[1]), .Kbd_Available(KDB[2]), .RAM_In_0(I0),
    .Kbd_ASCII_Data(KDB_DATA), .RAM_In_1(I1), .TTY_Enable(TTY_EN), .RAM_In_2(I2), .RAM_In_3(I3),
    .TTY_ASCII_Data(TTY_DATA), .Reset(RST), .RAM_Out_0(ram_1_data_out_0), .Clock(CLK),
    .RAM_Out_1(ram_1_data_out_1), .Stop(halt), .RAM_Out_2(ram_1_data_out_2), .RAM_Out_3(ram_1_data_out_3),
    .Mask(Mask), .Read_Time(ram_1_read_time), .Write_Time(ram_1_write_time), .nRead_Write(R_W),
    .Chip_Select(CS));
  D_Flip_Flop d_ff_2 (.clk(CLK), .D(d_ff_1_q), .Qn(LCLR), .reset(Reset_out));  // open: Q, preset, en
  or or_1 (RST, LCLR, LoadRAM);
  Clock clock_1 (.out(CLK));
  Multiplexer #(.width(32), .enable("false")) multiplexer_1 (.in0(I0), .in1(LData), .out(RI0), .sel(LoadRAM));
  Multiplexer #(.width(32), .enable("false")) multiplexer_2 (.in0(I1), .in1(LData), .out(RI1), .sel(LoadRAM));
  Multiplexer #(.width(32), .enable("false")) multiplexer_3 (.in0(I2), .in1(LData), .out(RI2), .sel(LoadRAM));
  Multiplexer #(.width(32), .enable("false")) multiplexer_4 (.in0(I3), .in1(LData), .out(RI3), .sel(LoadRAM));
  and and_1 (LoadRAM, ~DESHABILITAR_DISPATCHER, LoadRAMOn);  // AND_Gate
  Multiplexer #(.width(16), .enable("false")) multiplexer_5 (.in0(Addr), .in1(LAddr), .out(RAddr), .sel(LoadRAM));
  Multiplexer #(.width(4), .enable("false")) multiplexer_6 (.in0(Mask), .in1(LMask), .out(RMask), .sel(LoadRAM));
  Multiplexer #(.enable("false")) multiplexer_7 (.in0(CS), .in1(LW), .out(RCS), .sel(LoadRAM));
  Multiplexer #(.enable("false")) multiplexer_8 (.in0(R_W), .in1(LW), .out(R_R_W), .sel(LoadRAM));

  // Notes on the sheet:
  //   NO MODIFICAR
  //   Keyboard
endmodule

module RAM (
  input  [15:0] Address,
  input  [31:0] Data_In_0,
  input  [31:0] Data_In_1,
  input  [31:0] Data_In_2,
  input  [31:0] Data_In_3,
  input  [3:0] Mask,
  input  nRead_Write,
  input  Chip_Select,
  input  Reset,
  output [31:0] Data_Out_0,
  output [31:0] Data_Out_1,
  output [31:0] Data_Out_2,
  output [31:0] Data_Out_3,
  output [3:0] Read_Time,
  output [3:0] Write_Time
);

  wire and_2_out, and_3_out, and_4_out, and_5_out, and_6_out, and_7_out, and_8_out, and_9_out, Changed, CLK,
       comparator_2_eq, comparator_3_eq, comparator_4_eq, comparator_5_eq, comparator_6_eq, Count,
       demultiplexer_3_out0, Idle, Idle_q, Load, Load0, Load1, nand_1_out, or_1_out, or_2_out, or_3_out,
       or_4_out, or_5_out, or_6_out, or_7_out, or_8_out, or_9_out, or_10_out, Proc_q, Update_Mem, Zero_Time;
  wire [3:0] counter_1_q, multiplexer_1_out, subtractor_1_out;
  wire [31:0] register_1_q, register_2_q, register_3_q, register_4_q, register_5_q;

  // Probe on 4'b0011
  // Probe on 4'b0010
  Multiplexer #(.width(4), .enable("false")) multiplexer_1 (
    .in0(4'b0011), .in1(4'b0010), .out(multiplexer_1_out), .sel(nRead_Write));
  or or_1 (or_1_out, Idle, Update_Mem);
  or or_2 (or_2_out, ~Chip_Select, Reset);  // OR_Gate
  Subtractor #(.width(4)) subtractor_1 (.a(multiplexer_1_out), .b(4'b0010), .out(subtractor_1_out));  // open: bin, bout
  Demultiplexer #(.enable("false")) demultiplexer_1 (.out0(Idle), .out1(Load0), .in(Idle_q), .sel(Changed));
  D_Flip_Flop u_Idle (.clk(CLK), .D(or_1_out), .Q(Idle_q), .preset(or_2_out));  // open: Qn, en, reset
  // Probe on counter_1_q
  Counter #(.width(4), .max('hf)) counter_1 (
    .load(Load), .D(subtractor_1_out), .count(Count), .Q(counter_1_q), .clk(CLK), .clr(or_3_out));  // open: carry
  or or_3 (or_3_out, ~Chip_Select, Reset);  // OR_Gate
  Comparator #(.width(4), .mode("unsigned")) comparator_1 (
    .a(4'b0000), .b(counter_1_q), .eq(Zero_Time));  // open: gt, lt
  or or_4 (or_4_out, Count, Load0, Load1);
  Register #(.width(32)) register_1 (.D(Data_In_0), .en(Chip_Select), .Q(register_1_q), .clk(CLK), .clr(or_5_out));
  or or_5 (or_5_out, ~Chip_Select, Reset);  // OR_Gate
  Register #(.width(32)) register_2 (.D(Data_In_1), .en(Chip_Select), .Q(register_2_q), .clk(CLK), .clr(or_6_out));
  or or_6 (or_6_out, ~Chip_Select, Reset);  // OR_Gate
  Register #(.width(32)) register_3 (.D(Data_In_2), .en(Chip_Select), .Q(register_3_q), .clk(CLK), .clr(or_7_out));
  or or_7 (or_7_out, ~Chip_Select, Reset);  // OR_Gate
  Register #(.width(32)) register_4 (.D(Data_In_3), .en(Chip_Select), .Q(register_4_q), .clk(CLK), .clr(or_8_out));
  or or_8 (or_8_out, ~Chip_Select, Reset);  // OR_Gate
  Register #(.width(32)) register_5 (
    .D({{11{1'b1}}, nRead_Write, Mask, Address}), .en(Chip_Select), .Q(register_5_q), .clk(CLK),
    .clr(or_9_out));
  or or_9 (or_9_out, ~Chip_Select, Reset);  // OR_Gate
  D_Flip_Flop Proc (.clk(CLK), .D(or_4_out), .Q(Proc_q), .reset(or_10_out));  // open: Qn, preset, en
  or or_10 (or_10_out, ~Chip_Select, Reset);  // OR_Gate
  Demultiplexer #(.enable("false")) demultiplexer_2 (
    .out0(Count), .out1(Update_Mem), .in(demultiplexer_3_out0), .sel(Zero_Time));
  Demultiplexer #(.enable("false")) demultiplexer_3 (
    .out0(demultiplexer_3_out0), .out1(Load1), .in(Proc_q), .sel(Changed));
  Clock clock_1 (.out(CLK));
  Comparator #(.width(32)) comparator_2 (.a(register_1_q), .b(Data_In_0), .eq(comparator_2_eq));  // open: gt, lt
  Comparator #(.width(32)) comparator_3 (.a(register_2_q), .b(Data_In_1), .eq(comparator_3_eq));  // open: gt, lt
  Comparator #(.width(32)) comparator_4 (.a(register_3_q), .b(Data_In_2), .eq(comparator_4_eq));  // open: gt, lt
  Comparator #(.width(32)) comparator_5 (.a(register_4_q), .b(Data_In_3), .eq(comparator_5_eq));  // open: gt, lt
  Comparator #(.width(32)) comparator_6 (
    .a(register_5_q), .b({{11{1'b1}}, nRead_Write, Mask, Address}), .eq(comparator_6_eq));  // open: gt, lt
  nand nand_1 (nand_1_out, comparator_6_eq, comparator_2_eq, comparator_3_eq, comparator_4_eq, comparator_5_eq);
  and and_1 (Changed, nand_1_out, Chip_Select);
  or or_11 (Load, Count, Load1, Load0);
  and and_2 (and_2_out, Mask[0], Update_Mem, nRead_Write);
  and and_3 (and_3_out, Mask[1], Update_Mem, nRead_Write);
  and and_4 (and_4_out, Mask[2], Update_Mem, nRead_Write);
  and and_5 (and_5_out, Mask[3], Update_Mem, nRead_Write);
  RAM_part #(.addrWidth(16), .dataWidth(32), .bus("separate")) ram_1 (
    .addr(Address), .din(Data_In_0), .data(Data_Out_0), .str(and_2_out), .sel(Chip_Select), .clk(CLK),
    .ld(and_6_out), .clr(Reset));
  and and_6 (and_6_out, ~nRead_Write, Idle);  // AND_Gate
  RAM_part #(.addrWidth(16), .dataWidth(32), .bus("separate")) ram_2 (
    .addr(Address), .din(Data_In_1), .data(Data_Out_1), .str(and_3_out), .sel(Chip_Select), .clk(CLK),
    .ld(and_7_out), .clr(Reset));
  and and_7 (and_7_out, ~nRead_Write, Idle);  // AND_Gate
  RAM_part #(.addrWidth(16), .dataWidth(32), .bus("separate")) ram_3 (
    .addr(Address), .din(Data_In_2), .data(Data_Out_2), .str(and_4_out), .sel(Chip_Select), .clk(CLK),
    .ld(and_8_out), .clr(Reset));
  and and_8 (and_8_out, ~nRead_Write, Idle);  // AND_Gate
  RAM_part #(.addrWidth(16), .dataWidth(32), .bus("separate")) ram_4 (
    .addr(Address), .din(Data_In_3), .data(Data_Out_3), .str(and_5_out), .sel(Chip_Select), .clk(CLK),
    .ld(and_9_out), .clr(Reset));
  and and_9 (and_9_out, ~nRead_Write, Idle);  // AND_Gate

  assign Read_Time = 4'b0011;
  assign Write_Time = 4'b0010;

  // Other names for the same wires on the sheet: M0 = Mask[0]; M1 = Mask[1]; M2 = Mask[2]; M3 = Mask[3];
  //   RW = nRead_Write; CLR = Reset; CS = Chip_Select; Load2 = Count

  // Notes on the sheet:
  //   NO MODIFICAR
  //   excepto quizás los valores RT y WT
  //   BANK0
  //   BANK1
  //   BANK2
  //   BANK3
endmodule

module S_MIPS (
  input  Kbd_Available,
  input  [6:0] Kbd_ASCII_Data,
  input  [31:0] RAM_Out_0,
  input  [31:0] RAM_Out_1,
  input  Reset,
  input  [31:0] RAM_Out_2,
  input  Clock,
  input  [31:0] RAM_Out_3,
  input  [3:0] Read_Time,
  input  [3:0] Write_Time,
  output Kbd_Enable,
  output [15:0] Address,
  output Kbd_Clear,
  output TTY_Enable,
  output [6:0] TTY_ASCII_Data,
  output Stop,
  output [31:0] RAM_In_0,
  output [31:0] RAM_In_1,
  output [31:0] RAM_In_2,
  output [31:0] RAM_In_3,
  output [3:0] Mask,
  output nRead_Write,
  output Chip_Select
);

  wire BANK____0, cu_1_out_15, cu_1_out_17, cu_1_out_20, cu_1_out_21, cu_1_out_22, cu_1_out_24, cu_1_out_27,
       cu_1_out_28, cu_1_out_29, cu_1_out_31, cu_1_out_32, cu_1_out_34, cu_1_out_35, cu_1_out_37,
       cu_1_out_38, cu_1_out_39, cu_1_out_40, data_path_1_out_26, data_path_1_out_27, data_path_1_out_28,
       data_path_1_out_29, data_path_1_out_35, data_path_1_out_37, RAM_READ, RAM_WRITE, RESET_READ,
       RESET_WRITE;
  wire [1:0] cu_1_out_16, cu_1_out_18, cu_1_out_25, data_path_1_out_34, RAM_BANK;
  wire [2:0] cu_1_out_41, data_path_1_out_32;
  wire [31:0] ADDR, byte_rev_2_out, CURRENT_BANK, multiplexer_1_out, RAM_IN;

  Decoder #(.select(2), .disabled(0), .enable("false")) decoder_1 (
    .out0(Mask[0]), .out1(Mask[1]), .out2(Mask[2]), .out3(Mask[3]), .sel(RAM_BANK));
  Multiplexer #(.select(2), .width(32), .disabled(0), .enable("false")) multiplexer_1 (
    .in0(RAM_Out_0), .in1(RAM_Out_1), .in2(RAM_Out_2), .in3(RAM_Out_3), .out(multiplexer_1_out),
    .sel(RAM_BANK));
  Comparator #(.width(2), .mode("unsigned")) comparator_1 (.a(RAM_BANK), .b(2'b00), .eq(BANK____0));  // open: gt, lt
  MEM_PARSE mem_parse_1 (.IN(ADDR), .BANK(RAM_BANK), .ADDR(Address));
  DELAY delay_1 (.TIME(Read_Time), .Q(RAM_READ), .CLK(Clock), .RST(RESET_READ));
  DELAY delay_2 (.TIME(Write_Time), .Q(RAM_WRITE), .CLK(Clock), .RST(RESET_WRITE));
  BYTE_REV byte_rev_1 (.IN(multiplexer_1_out), .OUT(CURRENT_BANK));
  Demultiplexer #(.select(2), .width(32), .enable("false")) demultiplexer_1 (
    .out0(RAM_In_0), .out1(RAM_In_1), .out2(RAM_In_2), .out3(RAM_In_3), .in(byte_rev_2_out), .sel(RAM_BANK));
  BYTE_REV byte_rev_2 (.IN(RAM_IN), .OUT(byte_rev_2_out));
  CU cu_1 (
    .out_15(cu_1_out_15), .out_16(cu_1_out_16), .in_1(Clock), .in_2(data_path_1_out_26),
    .out_17(cu_1_out_17), .out_18(cu_1_out_18), .in_3(Reset), .out_20(cu_1_out_20), .out_21(cu_1_out_21),
    .out_22(cu_1_out_22), .in_4(RAM_READ), .in_5(data_path_1_out_27), .out_24(cu_1_out_24),
    .out_25(cu_1_out_25), .in_6(RAM_WRITE), .out_27(cu_1_out_27), .out_28(cu_1_out_28),
    .in_8(data_path_1_out_32), .in_9(data_path_1_out_29), .out_29(cu_1_out_29), .out_31(cu_1_out_31),
    .out_32(cu_1_out_32), .in_10(data_path_1_out_34), .in_11(Kbd_Available), .out_34(cu_1_out_34),
    .out_35(cu_1_out_35), .in_12(data_path_1_out_35), .in_13(Stop), .out_37(cu_1_out_37),
    .out_39(cu_1_out_39), .out_40(cu_1_out_40), .in_7(data_path_1_out_28), .out_19(TTY_Enable),
    .out_23(Kbd_Enable), .out_30(Chip_Select), .out_26(nRead_Write), .out_41(cu_1_out_41),
    .out_33(RESET_READ), .out_36(RESET_WRITE), .in_14(data_path_1_out_37), .out_38(cu_1_out_38));
  DATA_PATH data_path_1 (
    .out_26(data_path_1_out_26), .in_1(cu_1_out_15), .CURRENT_BANK(CURRENT_BANK), .in_3(cu_1_out_17),
    .in_4(cu_1_out_20), .out_27(data_path_1_out_27), .CLR(Reset), .in_6(cu_1_out_22), .CLK(Clock),
    .out_28(data_path_1_out_28), .in_8(cu_1_out_24), .in_9(cu_1_out_27), .out_29(data_path_1_out_29),
    .in_10(cu_1_out_31), .in_11(cu_1_out_16), .in_12(cu_1_out_29), .out_31(Stop), .in_13(cu_1_out_35),
    .in_14(cu_1_out_18), .in_15(cu_1_out_32), .out_32(data_path_1_out_32), .in_16(cu_1_out_34),
    .in_17(Kbd_ASCII_Data), .in_18(cu_1_out_21), .in_19(cu_1_out_37), .out_34(data_path_1_out_34),
    .in_20(cu_1_out_39), .in_21(cu_1_out_25), .in_22(cu_1_out_40), .out_35(data_path_1_out_35),
    .in_24(cu_1_out_28), .out_30(TTY_ASCII_Data), .out_33(ADDR), .out_36(RAM_IN), .in_25(cu_1_out_41),
    .in_23(cu_1_out_38), .out_37(data_path_1_out_37));

  // Other names for the same wires on the sheet: CLK = Clock; CLR = Reset; CS = Chip_Select;
  //   KBD_AVAIL = Kbd_Available; KBD_CLR = Kbd_Clear; KBD_DATA[6:0] = Kbd_ASCII_Data; RAM_A[15:0] = Address;
  //   RAM_INPUT_0[31:0] = RAM_In_0; RAM_INPUT_1[31:0] = RAM_In_1; RAM_INPUT_2[31:0] = RAM_In_2;
  //   RAM_INPUT_3[31:0] = RAM_In_3; RAM_MASK[3:0] = Mask; RAM_OUTPUT_0[31:0] = RAM_Out_0;
  //   RAM_OUTPUT_1[31:0] = RAM_Out_1; RAM_OUTPUT_2[31:0] = RAM_Out_2; RAM_OUTPUT_3[31:0] = RAM_Out_3;
  //   RW = nRead_Write; TTY_DATA[6:0] = TTY_ASCII_Data

  // Notes on the sheet:
  //   RAM ADDRESS
  //   DATA FROM RAM
  //   DATA TO RAM
  //   DATA WRITE MASK
  //   RAM TIMING
  //   RAM CONTROL
  //   KEYBOARD
  //   TTY
  //   SEQUENCING
endmodule

module RAM_Dispatcher (
  input  [3:0] WriteTime,
  input  Clock,
  input  CLR,
  output [31:0] Data,
  output [15:0] Address,
  output [3:0] Mask,
  output Finished,
  output Write
);

  wire demultiplexer_2_out1, demultiplexer_3_out1, End, IDLE_q, IncAddr, Load, or_1_out, or_2_out, While_q,
       WriteEnd;
  wire [3:0] counter_1_q;
  wire [31:0] CurrentAddress_q;

  Counter #(.width(32), .max('hffffffff)) CurrentAddress (
    .count(IncAddr), .Q({CurrentAddress_q[31:18], Address, CurrentAddress_q[1:0]}), .clk(Clock), .clr(CLR));  // open: load, D, carry
  or or_1 (or_1_out, IncAddr, demultiplexer_3_out1, Finished);
  D_Flip_Flop IDLE (.clk(Clock), .D(or_1_out), .Q(IDLE_q), .preset(CLR));  // open: Qn, en, reset
  Demultiplexer #(.enable("false")) demultiplexer_1 (.out0(Load), .out1(Finished), .in(IDLE_q), .sel(End));
  D_Flip_Flop While (.clk(Clock), .D(or_2_out), .Q(While_q), .reset(CLR));  // open: Qn, preset, en
  or or_2 (or_2_out, Write, Load);
  RAM_part #(.addrWidth(18), .dataWidth(32)) ram_1 (
    .addr({Address, CurrentAddress_q[1:0]}), .data(Data), .clk(Clock));  // open: sel, ld, clr
  Demultiplexer #(.enable("false")) demultiplexer_2 (
    .out0(Write), .out1(demultiplexer_2_out1), .in(While_q), .sel(WriteEnd));
  Decoder #(.select(2)) decoder_1 (
    .out0(Mask[0]), .out1(Mask[1]), .out2(Mask[2]), .out3(Mask[3]), .sel(CurrentAddress_q[1:0]));  // open: en
  Demultiplexer #(.enable("false")) demultiplexer_3 (
    .out0(IncAddr), .out1(demultiplexer_3_out1), .in(demultiplexer_2_out1), .sel(End));
  Counter #(.width(4), .max('hf)) counter_1 (
    .load(Load), .D(WriteTime), .count(Write), .Q(counter_1_q), .clk(Clock));  // open: carry, clr
  Comparator #(.width(32)) comparator_1 (.a(Data), .b({32{1'b1}}), .eq(End));  // open: gt, lt
  Comparator #(.width(4)) comparator_2 (.a(4'b0000), .b(counter_1_q), .eq(WriteEnd));  // open: gt, lt

  // Other names for the same wires on the sheet: CLK = Clock; Count = Write; WT[3:0] = WriteTime
endmodule

module RF (
  input  WRITE,
  input  [31:0] IN,
  input  [4:0] SEL,
  input  CLK,
  input  RST,
  input  [31:0] SP_IN,
  output [31:0] OUT,
  output [31:0] SP_OUT
);

  wire and_1_out, comparator_1_eq, R1I, R2I, R3I, R4I, R5I, R6I, R7I, R8I, R9I, R10I, R11I, R12I, R13I, R14I,
       R15I, R16I, R17I, R18I, R19I, R20I, R21I, R22I, R23I, R24I, R25I, R26I, R27I, R28I, R29I, R30I,
       undriven;
  wire [31:0] R1O, R2O, R3O, R4O, R5O, R6O, R7O, R8O, R9O, R10O, R11O, R12O, R13O, R14O, R15O, R16O, R17O,
       R18O, R19O, R20O, R21O, R22O, R23O, R24O, R25O, R26O, R27O, R28O, R29O, R30O, R31I;

  Comparator #(.width(5), .mode("unsigned")) comparator_1 (
    .a({5{1'b1}}), .b(SEL), .eq(comparator_1_eq));  // open: gt, lt
  Multiplexer #(.width(32), .enable("false")) multiplexer_1 (.in0(SP_IN), .in1(IN), .out(R31I), .sel(and_1_out));
  and and_1 (and_1_out, comparator_1_eq, WRITE);
  Register #(.width(32)) R4 (.D(IN), .en(R4I), .Q(R4O), .clk(CLK), .clr(RST));
  Register #(.width(32)) R1 (.D(IN), .en(R1I), .Q(R1O), .clk(CLK), .clr(RST));
  Register #(.width(32)) R5 (.D(IN), .en(R5I), .Q(R5O), .clk(CLK), .clr(RST));
  Decoder #(.select(5), .disabled(0)) decoder_1 (
    .out1(R1I), .out2(R2I), .out3(R3I), .out4(R4I), .out5(R5I), .out6(R6I), .out7(R7I), .out8(R8I),
    .out9(R9I), .out10(R10I), .out11(R11I), .out12(R12I), .out13(R13I), .out14(R14I), .out15(R15I),
    .out16(R16I), .out17(R17I), .out18(R18I), .out19(R19I), .out20(R20I), .out21(R21I), .out22(R22I),
    .out23(R23I), .out24(R24I), .out25(R25I), .out26(R26I), .out27(R27I), .out28(R28I), .out29(R29I),
    .out30(R30I), .sel(SEL), .en(WRITE));  // open: out0, out31
  Register #(.width(32)) R3 (.D(IN), .en(R3I), .Q(R3O), .clk(CLK), .clr(RST));
  Register #(.width(32)) R2 (.D(IN), .en(R2I), .Q(R2O), .clk(CLK), .clr(RST));
  Register #(.width(32)) R6 (.D(IN), .en(R6I), .Q(R6O), .clk(CLK), .clr(RST));
  Register #(.width(32)) R7 (.D(IN), .en(R7I), .Q(R7O), .clk(CLK), .clr(RST));
  Register #(.width(32)) R8 (.D(IN), .en(R8I), .Q(R8O), .clk(CLK), .clr(RST));
  Register #(.width(32)) R12 (.D(IN), .en(R12I), .Q(R12O), .clk(CLK), .clr(RST));
  Register #(.width(32)) R9 (.D(IN), .en(R9I), .Q(R9O), .clk(CLK), .clr(RST));
  Register #(.width(32)) R13 (.D(IN), .en(R13I), .Q(R13O), .clk(CLK), .clr(RST));
  Register #(.width(32)) R10 (.D(IN), .en(R10I), .Q(R10O), .clk(CLK), .clr(RST));
  Register #(.width(32)) R14 (.D(IN), .en(R14I), .Q(R14O), .clk(CLK), .clr(RST));
  Register #(.width(32)) R11 (.D(IN), .en(R11I), .Q(R11O), .clk(CLK), .clr(RST));
  Register #(.width(32)) R15 (.D(IN), .en(R15I), .Q(R15O), .clk(CLK), .clr(RST));
  Register #(.width(32)) R16 (.D(IN), .en(R16I), .Q(R16O), .clk(CLK), .clr(RST));
  Register #(.width(32)) _20R (.D(IN), .en(undriven), .Q(R20O), .clk(CLK), .clr(RST));
  Register #(.width(32)) R17 (.D(IN), .en(R17I), .Q(R17O), .clk(CLK), .clr(RST));
  Register #(.width(32)) R21 (.D(IN), .en(R21I), .Q(R21O), .clk(CLK), .clr(RST));
  Register #(.width(32)) R18 (.D(IN), .en(R18I), .Q(R18O), .clk(CLK), .clr(RST));
  Register #(.width(32)) R22 (.D(IN), .en(R22I), .Q(R22O), .clk(CLK), .clr(RST));
  Register #(.width(32)) R19 (.D(IN), .en(R19I), .Q(R19O), .clk(CLK), .clr(RST));
  Register #(.width(32)) R23 (.D(IN), .en(R23I), .Q(R23O), .clk(CLK), .clr(RST));
  Register #(.width(32)) R25 (.D(IN), .en(R25I), .Q(R25O), .clk(CLK), .clr(RST));
  Register #(.width(32)) R24 (.D(IN), .en(R24I), .Q(R24O), .clk(CLK), .clr(RST));
  Register #(.width(32)) R28 (.D(IN), .en(R28I), .Q(R28O), .clk(CLK), .clr(RST));
  Register #(.width(32)) R29 (.D(IN), .en(R29I), .Q(R29O), .clk(CLK), .clr(RST));
  Register #(.width(32)) R26 (.D(IN), .en(R26I), .Q(R26O), .clk(CLK), .clr(RST));
  Register #(.width(32)) R30 (.D(IN), .en(R30I), .Q(R30O), .clk(CLK), .clr(RST));
  Register #(.width(32)) R27 (.D(IN), .en(R27I), .Q(R27O), .clk(CLK), .clr(RST));
  Register #(.width(32)) R31 (.D(R31I), .Q(SP_OUT), .clk(CLK), .clr(RST));  // open: en
  Multiplexer #(.select(5), .width(32), .enable("false")) multiplexer_2 (
    .in0({32{1'b0}}), .in1(R1O), .in2(R2O), .in3(R3O), .in4(R4O), .in5(R5O), .in6(R6O), .in7(R7O), .in8(R8O),
    .in9(R9O), .in10(R10O), .in11(R11O), .in12(R12O), .in13(R13O), .in14(R14O), .in15(R15O), .in16(R16O),
    .in17(R17O), .in18(R18O), .in19(R19O), .in20(R20O), .in21(R21O), .in22(R22O), .in23(R23O), .in24(R24O),
    .in25(R25O), .in26(R26O), .in27(R27O), .in28(R28O), .in29(R29O), .in30(R30O), .in31(SP_OUT), .out(OUT),
    .sel(SEL));

  // Other names for the same wires on the sheet: INPUT[31:0] = IN; R31O[31:0] = SP_OUT; RESET = RST;
  //   SP_IN_t[31:0] = R31I; W = WRITE
endmodule

module ALU (
  input  [31:0] IN_A,
  input  [31:0] IN_B,
  input  U,
  input  [2:0] SEL,
  input  START,
  input  CLK,
  output [31:0] OUT1,
  output [31:0] OUT2,
  output out_9,
  output out_10
);

  wire abs_1_sf, abs_2_sf, comparator_1_lt, comparator_2_lt, decoder_1_out0, decoder_1_out1, MUL_DONE,
       multiplexer_1_out, or_2_out, xor_2_out;
  wire [31:0] abs_1_out, abs_2_out, ADD_OUT, AND_OUT, DIV_OUT1, DIV_OUT_2, divider_2_out, MUL_OUT1,
       MUL_OUT_2, multiplexer_4_out, multiplexer_5_out, multiplexer_6_out, multiplexer_7_out, negator_1_out,
       negator_2_out, NOR_OUT, OR_OUT, SUB_OUT, U_DIV_OUT1, U_DIV_OUT_2, U_MUL_OUT1, U_MUL_OUT_2, XOR_OUT;

  Adder #(.width(32)) adder_1 (.a(IN_A), .b(IN_B), .out(ADD_OUT));  // open: cin, cout
  Subtractor #(.width(32)) subtractor_1 (.a(IN_A), .b(IN_B), .out(SUB_OUT));  // open: bin, bout
  Multiplier #(.width(32)) multiplier_1 (.a(IN_A), .b(IN_B), .out(MUL_OUT1), .cout(MUL_OUT_2));  // open: cin
  Divider #(.width(32)) divider_1 (.a(IN_A), .b(IN_B), .out(U_DIV_OUT1), .rem(U_DIV_OUT_2));  // open: upper
  UMUL_A umul_a_1 (
    .IN_A(IN_A), .IN_B(IN_B), .START(START), .CLK(CLK), .OUT_Lo(U_MUL_OUT1), .OUT_Hi(U_MUL_OUT_2),
    .out_7(MUL_DONE));
  Multiplexer #(.select(3), .enable("false")) multiplexer_1 (
    .in0(1'b1), .in1(1'b1), .in2(MUL_DONE), .in3(1'b1), .in4(1'b1), .in5(1'b1), .in6(1'b1), .in7(1'b1),
    .out(multiplexer_1_out), .sel(SEL));
  assign AND_OUT = IN_A & IN_B;  // AND_Gate and_1, 32 bits wide
  assign OR_OUT = IN_A | IN_B;  // OR_Gate or_1, 32 bits wide
  assign NOR_OUT = ~OR_OUT;  // NOT_Gate not_1, 32 bits wide
  assign XOR_OUT = IN_A ^ IN_B;  // XOR_Gate xor_1, 32 bits wide
  or or_2 (or_2_out, multiplexer_1_out, ~U);  // OR_Gate
  ABS abs_1 (.IN(IN_A), .OUT(abs_1_out), .SF(abs_1_sf));
  ABS abs_2 (.IN(IN_B), .OUT(abs_2_out), .SF(abs_2_sf));
  and and_2 (out_10, or_2_out, ~START);  // AND_Gate
  Divider #(.width(32)) divider_2 (.a(abs_1_out), .b(abs_2_out), .out(divider_2_out), .rem(DIV_OUT_2));  // open: upper
  xor xor_2 (xor_2_out, abs_1_sf, abs_2_sf);
  Negator #(.width(32)) negator_1 (.in(divider_2_out), .out(negator_1_out));
  Negator #(.width(32)) negator_2 (.in(DIV_OUT_2), .out(negator_2_out));
  Multiplexer #(.width(32), .enable("false")) multiplexer_2 (
    .in0(divider_2_out), .in1(negator_1_out), .out(DIV_OUT1), .sel(xor_2_out));
  Multiplexer #(.width(32), .enable("false")) multiplexer_3 (.in1(negator_2_out), .sel(xor_2_out));  // open: in0, out
  Multiplexer #(.width(32), .enable("false")) multiplexer_4 (
    .in0(MUL_OUT1), .in1(U_MUL_OUT1), .out(multiplexer_4_out), .sel(U));
  Multiplexer #(.width(32), .enable("false")) multiplexer_5 (
    .in0(DIV_OUT1), .in1(U_DIV_OUT1), .out(multiplexer_5_out), .sel(U));
  Multiplexer #(.width(32), .enable("false")) multiplexer_6 (
    .in0(DIV_OUT_2), .in1(U_DIV_OUT_2), .out(multiplexer_6_out), .sel(U));
  Multiplexer #(.width(32), .enable("false")) multiplexer_7 (
    .in0(MUL_OUT_2), .in1(U_MUL_OUT_2), .out(multiplexer_7_out), .sel(U));
  Decoder #(.enable("false")) decoder_1 (.out0(decoder_1_out0), .out1(decoder_1_out1), .sel(SEL[2]));
  Comparator #(.width(32)) comparator_1 (.a(IN_A), .b(IN_B), .lt(comparator_1_lt));  // open: gt, eq
  Comparator #(.width(32), .mode("unsigned")) comparator_2 (.a(IN_A), .b(IN_B), .lt(comparator_2_lt));  // open: gt, eq
  Multiplexer #(.select(2), .width(32)) multiplexer_8 (
    .in0(ADD_OUT), .in1(SUB_OUT), .in2(multiplexer_4_out), .in3(multiplexer_5_out), .out(OUT1),
    .sel(SEL[1:0]), .en(decoder_1_out0));
  Multiplexer #(.width(32)) multiplexer_9 (
    .in0(multiplexer_7_out), .in1(multiplexer_6_out), .out(OUT2), .sel(SEL[0]), .en(decoder_1_out0));
  Multiplexer #(.select(2), .width(32)) multiplexer_10 (
    .in0(AND_OUT), .in1(OR_OUT), .in2(NOR_OUT), .in3(XOR_OUT), .out(OUT1), .sel(SEL[1:0]), .en(decoder_1_out1));
  Multiplexer #(.enable("false")) multiplexer_11 (.in0(comparator_1_lt), .in1(comparator_2_lt), .out(out_9), .sel(U));

  // Other names for the same wires on the sheet: DONE = out_10; LS = out_9

  // Notes on the sheet:
  //   SE PUSO ASI PARA QUE FUNCIONARA EL CASO DE PRUEBA
  //   EL RESTO DEBERIA PODER SER NEGATIVO AQUI
endmodule

module ID (
  input  [31:0] INSTRUCTION,
  input  EN,
  output [2:0] OP,
  output [1:0] OP_TYPE,
  output I,
  output U,
  output [4:0] out_7,
  output [4:0] out_8,
  output [4:0] out_9,
  output [25:0] out_10,
  output [15:0] out_11
);

  wire ADD, ADD0, ADD1, AND, AND0, AND1, BEQ, BGTZ, BLEZ, BLTZ, BNE, comparator_1_eq, comparator_2_eq,
       comparator_3_eq, comparator_4_eq, comparator_5_eq, comparator_6_eq, comparator_7_eq, comparator_10_eq,
       comparator_11_eq, comparator_12_eq, comparator_13_eq, comparator_14_eq, comparator_15_eq,
       comparator_16_eq, comparator_17_eq, comparator_18_eq, comparator_19_eq, comparator_23_eq,
       comparator_24_eq, comparator_25_eq, comparator_26_eq, comparator_27_eq, comparator_28_eq,
       comparator_29_eq, DIV, DIVU, HALT, JMP, JMPR, KBD, LW, MFHI, MFLO, MUL, MULU, NOP, NOR, OP0, OP1, OP2,
       OP3, OP4, OP5, OP6, OP7, OPC_0, OPT0, OPT1, OPT2, OPT3, OR, OR0, OR1, or_1_out, or_2_out, or_3_out,
       POP, PUSH, RND, SLT, SLT0, SLT1, SLT2, SLTI, SLTU, SLTU0, SUB, SW, TTY, XOR0, XOR1;
  wire [5:0] FUNC___1;

  Priority_Encoder #(.select(2)) priority_encoder_1 (
    .in0(OPT0), .in1(OPT1), .in2(OPT2), .in3(OPT3), .out(OP_TYPE), .en_in(EN));  // open: gs, en_out
  Priority_Encoder priority_encoder_2 (
    .in0(OP0), .in1(OP1), .in2(OP2), .in3(OP3), .in4(OP4), .in5(OP5), .in6(OP6), .in7(OP7), .out(OP),
    .en_in(EN));  // open: gs, en_out
  Comparator #(.width(6), .mode("unsigned")) comparator_1 (
    .a(INSTRUCTION[31:26]), .b({6{1'b1}}), .eq(comparator_1_eq));  // open: gt, lt
  Comparator #(.width(6), .mode("unsigned")) comparator_2 (
    .a(INSTRUCTION[5:0]), .b({6{1'b1}}), .eq(comparator_2_eq));  // open: gt, lt
  Comparator #(.width(6), .mode("unsigned")) comparator_3 (
    .a(INSTRUCTION[5:0]), .b(6'b000001), .eq(comparator_3_eq));  // open: gt, lt
  Comparator #(.width(6), .mode("unsigned")) comparator_4 (
    .a(INSTRUCTION[5:0]), .b(6'b000010), .eq(comparator_4_eq));  // open: gt, lt
  Comparator #(.width(6), .mode("unsigned")) comparator_5 (
    .a(INSTRUCTION[5:0]), .b(6'b000100), .eq(comparator_5_eq));  // open: gt, lt
  and and_1 (HALT, comparator_1_eq, comparator_2_eq);
  and and_2 (TTY, comparator_1_eq, comparator_3_eq);
  and and_3 (RND, comparator_1_eq, comparator_4_eq);
  and and_4 (KBD, comparator_1_eq, comparator_5_eq);
  Subtractor #(.width(6)) subtractor_1 (.a(INSTRUCTION[5:0]), .b(6'b000001), .out(FUNC___1));  // open: bin, bout
  Comparator #(.width(6), .mode("unsigned")) comparator_6 (
    .a(INSTRUCTION[5:0]), .b(6'b010000), .eq(comparator_6_eq));  // open: gt, lt
  Comparator #(.width(6), .mode("unsigned")) comparator_7 (
    .a(INSTRUCTION[5:0]), .b(6'b001000), .eq(comparator_7_eq));  // open: gt, lt
  Comparator #(.width(6), .mode("unsigned")) comparator_8 (
    .a(INSTRUCTION[31:26]), .b(6'b000010), .eq(JMP));  // open: gt, lt
  Comparator #(.width(6), .mode("unsigned")) comparator_9 (
    .a(INSTRUCTION[31:26]), .b({6{1'b0}}), .eq(OPC_0));  // open: gt, lt
  Comparator #(.width(6), .mode("unsigned")) comparator_10 (
    .a(INSTRUCTION[5:0]), .b({6{1'b0}}), .eq(comparator_10_eq));  // open: gt, lt
  Comparator #(.width(6), .mode("unsigned")) comparator_11 (
    .a(INSTRUCTION[5:0]), .b(6'b100000), .eq(comparator_11_eq));  // open: gt, lt
  Comparator #(.width(6), .mode("unsigned")) comparator_12 (
    .a(INSTRUCTION[5:0]), .b(6'b100010), .eq(comparator_12_eq));  // open: gt, lt
  Comparator #(.width(6), .mode("unsigned")) comparator_13 (
    .a(INSTRUCTION[5:0]), .b(6'b011000), .eq(comparator_13_eq));  // open: gt, lt
  or or_1 (or_1_out, comparator_13_eq, comparator_14_eq);
  Comparator #(.width(6), .mode("unsigned")) comparator_14 (
    .a(FUNC___1), .b(6'b011000), .eq(comparator_14_eq));  // open: gt, lt
  Comparator #(.width(6), .mode("unsigned")) comparator_15 (
    .a(INSTRUCTION[5:0]), .b(6'b011010), .eq(comparator_15_eq));  // open: gt, lt
  or or_2 (or_2_out, comparator_15_eq, comparator_16_eq);
  Comparator #(.width(6), .mode("unsigned")) comparator_16 (
    .a(FUNC___1), .b(6'b011010), .eq(comparator_16_eq));  // open: gt, lt
  Comparator #(.width(6), .mode("unsigned")) comparator_17 (
    .a(INSTRUCTION[5:0]), .b(6'b101010), .eq(comparator_17_eq));  // open: gt, lt
  or or_3 (or_3_out, comparator_17_eq, comparator_18_eq);
  Comparator #(.width(6), .mode("unsigned")) comparator_18 (
    .a(FUNC___1), .b(6'b101010), .eq(comparator_18_eq));  // open: gt, lt
  and and_5 (MFHI, OPC_0, comparator_6_eq);
  and and_6 (JMPR, OPC_0, comparator_7_eq);
  and and_7 (NOP, OPC_0, comparator_10_eq);
  and and_8 (ADD0, OPC_0, comparator_11_eq);
  and and_9 (SUB, OPC_0, comparator_12_eq);
  and and_10 (MUL, OPC_0, or_1_out);
  and and_11 (MULU, MUL, comparator_14_eq);
  and and_12 (DIV, OPC_0, or_2_out);
  and and_13 (DIVU, DIV, comparator_16_eq);
  and and_14 (SLT0, OPC_0, or_3_out);
  and and_15 (SLTU0, SLT0, comparator_18_eq);
  or or_4 (OPT0, ADD, SUB, MUL, DIV, AND, OR, NOR, OP7);
  Comparator #(.width(6), .mode("unsigned")) comparator_19 (
    .a(INSTRUCTION[5:0]), .b(6'b010010), .eq(comparator_19_eq));  // open: gt, lt
  Comparator #(.width(6), .mode("unsigned")) comparator_20 (
    .a(INSTRUCTION[31:26]), .b(6'b000001), .eq(BLTZ));  // open: gt, lt
  Comparator #(.width(6), .mode("unsigned")) comparator_21 (
    .a(INSTRUCTION[31:26]), .b(6'b000111), .eq(BGTZ));  // open: gt, lt
  Comparator #(.width(6), .mode("unsigned")) comparator_22 (
    .a(INSTRUCTION[31:26]), .b(6'b000110), .eq(BLEZ));  // open: gt, lt
  or or_5 (OP0, ADD, SLT, BEQ, NOP);
  or or_6 (OP2, MUL, SW, BLEZ, TTY);
  or or_7 (OP4, AND, PUSH, BLTZ, KBD);
  Comparator #(.width(6), .mode("unsigned")) comparator_23 (
    .a(INSTRUCTION[5:0]), .b(6'b100100), .eq(comparator_23_eq));  // open: gt, lt
  Comparator #(.width(6), .mode("unsigned")) comparator_24 (
    .a(INSTRUCTION[5:0]), .b(6'b100101), .eq(comparator_24_eq));  // open: gt, lt
  and and_16 (MFLO, OPC_0, comparator_19_eq);
  or or_8 (OPT1, SLT, LW, SW, POP, PUSH, MFHI, MFLO);
  and and_17 (AND0, OPC_0, comparator_23_eq);
  and and_18 (OR0, OPC_0, comparator_24_eq);
  or or_9 (OP1, SUB, LW, BNE, HALT);
  or or_10 (OP3, DIV, POP, BGTZ, RND);
  or or_11 (OP5, OR, MFHI, JMP);
  Comparator #(.width(6), .mode("unsigned")) comparator_25 (
    .a(INSTRUCTION[5:0]), .b(6'b100111), .eq(comparator_25_eq));  // open: gt, lt
  Comparator #(.width(6), .mode("unsigned")) comparator_26 (
    .a(INSTRUCTION[5:0]), .b(6'b101000), .eq(comparator_26_eq));  // open: gt, lt
  Comparator #(.width(6), .mode("unsigned")) comparator_27 (
    .a(INSTRUCTION[31:26]), .b(6'b111000), .eq(comparator_27_eq));  // open: gt, lt
  Comparator #(.width(6), .mode("unsigned")) comparator_28 (
    .a(INSTRUCTION[5:0]), .b({6{1'b0}}), .eq(comparator_28_eq));  // open: gt, lt
  Comparator #(.width(6), .mode("unsigned")) comparator_29 (
    .a(FUNC___1), .b({6{1'b0}}), .eq(comparator_29_eq));  // open: gt, lt
  Comparator #(.width(6), .mode("unsigned")) comparator_30 (
    .a(INSTRUCTION[31:26]), .b(6'b100011), .eq(LW));  // open: gt, lt
  or or_12 (OP6, NOR, MFLO, JMPR);
  or or_13 (OPT2, BEQ, BNE, BLEZ, BGTZ, BLTZ, JMP, JMPR);
  and and_19 (NOR, OPC_0, comparator_25_eq);
  and and_20 (XOR0, OPC_0, comparator_26_eq);
  and and_21 (POP, comparator_27_eq, comparator_28_eq);
  and and_22 (PUSH, comparator_27_eq, comparator_29_eq);
  or or_14 (I, ADD1, SLTI, AND1, OR1, XOR1);
  or or_15 (U, MULU, DIVU, SLTU);
  or or_16 (OR, OR0, OR1);
  Comparator #(.width(6), .mode("unsigned")) comparator_31 (
    .a(INSTRUCTION[31:26]), .b(6'b101011), .eq(SW));  // open: gt, lt
  or or_17 (OPT3, NOP, HALT, TTY, RND, KBD);
  Comparator #(.width(6), .mode("unsigned")) comparator_32 (
    .a(INSTRUCTION[31:26]), .b(6'b001000), .eq(ADD1));  // open: gt, lt
  Comparator #(.width(6), .mode("unsigned")) comparator_33 (
    .a(INSTRUCTION[31:26]), .b(6'b001010), .eq(SLT1));  // open: gt, lt
  Comparator #(.width(6), .mode("unsigned")) comparator_34 (
    .a(INSTRUCTION[31:26]), .b(6'b000100), .eq(BEQ));  // open: gt, lt
  Comparator #(.width(6), .mode("unsigned")) comparator_35 (
    .a(INSTRUCTION[31:26]), .b(6'b000101), .eq(BNE));  // open: gt, lt
  or or_18 (AND, AND0, AND1);
  or or_19 (SLT, SLT0, SLT1, SLT2);
  or or_20 (SLTU, SLTU0, SLT2);
  or or_21 (OP7, XOR0, XOR1);
  or or_22 (ADD, ADD0, ADD1);
  or or_23 (SLTI, SLT1, SLT2);
  Comparator #(.width(6), .mode("unsigned")) comparator_36 (
    .a(INSTRUCTION[31:26]), .b(6'b001100), .eq(AND1));  // open: gt, lt
  Comparator #(.width(6), .mode("unsigned")) comparator_37 (
    .a(INSTRUCTION[31:26]), .b(6'b001101), .eq(OR1));  // open: gt, lt
  Comparator #(.width(6), .mode("unsigned")) comparator_38 (
    .a(INSTRUCTION[31:26]), .b(6'b001110), .eq(XOR1));  // open: gt, lt
  Comparator #(.width(6), .mode("unsigned")) comparator_39 (
    .a(INSTRUCTION[31:26]), .b(6'b001011), .eq(SLT2));  // open: gt, lt

  assign out_7 = INSTRUCTION[25:21];
  assign out_8 = INSTRUCTION[20:16];
  assign out_9 = INSTRUCTION[15:11];
  assign out_10 = INSTRUCTION[25:0];
  assign out_11 = INSTRUCTION[15:0];

  // Other names for the same wires on the sheet: ADDI = ADD1; ANDI = AND1; ENABLED = EN; IMDT = I;
  //   CONST[15:0] = INSTRUCTION[15:0]; INS[31:0] = INSTRUCTION; JUMP_DEST[25:0] = INSTRUCTION[25:0];
  //   R_FUNC_CODE[5:0] = INSTRUCTION[5:0]; ARG_3[4:0] = INSTRUCTION[15:11]; ARG_2[4:0] = INSTRUCTION[20:16];
  //   ARG_1[4:0] = INSTRUCTION[25:21]; OPCODE[5:0] = INSTRUCTION[31:26]; ORI = OR1; SLTI0 = SLT1; SLTI1 = SLT2;
  //   SLTU1 = SLT2; UNSIGNED = U; XOR = OP7; XORI = XOR1

  // Notes on the sheet:
  //   0 - Arithmetic & Logic
  //   1 - Memory
  //   2 - Flow Control
  //   3 - Specials
endmodule

module DELAY (
  input  [3:0] TIME,
  input  CLK,
  input  RST,
  output Q
);

  wire comparator_1_eq, or_1_out;
  wire [3:0] counter_1_q;

  Counter #(.width(4), .max('hf)) counter_1 (
    .Q(counter_1_q), .clk(CLK), .clr(or_1_out));  // open: load, D, count, carry
  or or_1 (or_1_out, comparator_1_eq, RST);
  Comparator #(.width(4), .mode("unsigned")) comparator_1 (
    .a(TIME), .b(counter_1_q), .eq(comparator_1_eq));  // open: gt, lt
  D_Flip_Flop d_ff_1 (.clk(CLK), .D(comparator_1_eq), .Q(Q), .preset(comparator_1_eq), .reset(RST));  // open: Qn, en
endmodule

module MEM_PARSE (
  input  [31:0] IN,
  output [1:0] BANK,
  output [15:0] ADDR
);


  assign ADDR = IN[19:4];
  assign BANK = IN[3:2];
endmodule

module ABS (
  input  [31:0] IN,
  output [31:0] OUT,
  output SF
);

  wire [31:0] negator_1_out;

  Multiplexer #(.width(32), .enable("false")) multiplexer_1 (.in0(IN), .in1(negator_1_out), .out(OUT), .sel(IN[31]));
  Negator #(.width(32)) negator_1 (.in(IN), .out(negator_1_out));

  assign SF = IN[31];
endmodule

module NEG_64 (
  input  [31:0] IN_A,
  input  [31:0] IN_B,
  output [31:0] OUT_A,
  output [31:0] OUT_B
);

  wire adder_1_cout;
  wire [31:0] not_1_out, not_2_out;

  assign not_1_out = ~IN_B;  // NOT_Gate not_1, 32 bits wide
  Adder #(.width(32)) adder_1 (.a(not_1_out), .b(32'h1), .out(OUT_B), .cout(adder_1_cout));  // open: cin
  assign not_2_out = ~IN_A;  // NOT_Gate not_2, 32 bits wide
  Adder #(.width(32)) adder_2 (.a(not_2_out), .b({32{1'b0}}), .out(OUT_A), .cin(adder_1_cout));  // open: cout
endmodule

module BYTE_REV (
  input  [31:0] IN,
  output [31:0] OUT
);


  assign OUT = {IN[7:0], IN[15:8], IN[23:16], IN[31:24]};
endmodule

module CU (
  input  in_1,
  input  in_2,
  input  in_3,
  input  in_4,
  input  in_5,
  input  in_6,
  input  in_7,
  input  [2:0] in_8,
  input  in_9,
  input  [1:0] in_10,
  input  in_11,
  input  in_12,
  input  in_13,
  input  in_14,
  output out_15,
  output [1:0] out_16,
  output out_17,
  output [1:0] out_18,
  output out_19,
  output out_20,
  output out_21,
  output out_22,
  output out_23,
  output out_24,
  output [1:0] out_25,
  output out_26,
  output out_27,
  output out_28,
  output out_29,
  output out_30,
  output out_31,
  output out_32,
  output out_33,
  output out_34,
  output out_35,
  output out_36,
  output out_37,
  output out_38,
  output out_39,
  output out_40,
  output [2:0] out_41
);

  wire A1____A2, ADR10, ADR11, BEQ, BGTZ, BLEZ, BLTZ, BNE, BRANCH, BRANCH0, BRANCH1, BRANCH2, BRANCH3,
       BRANCH4, CHANGE_TR_3_q, CS0, CS1, CS2, CS3, CS4, demultiplexer_1_out0, demultiplexer_1_out1,
       demultiplexer_1_out2, demultiplexer_1_out3, demultiplexer_1_out4, demultiplexer_1_out5,
       demultiplexer_1_out6, demultiplexer_1_out7, demultiplexer_3_out0, demultiplexer_4_out0,
       demultiplexer_4_out1, demultiplexer_5_out0, demultiplexer_6_out0, demultiplexer_7_out0,
       demultiplexer_10_out0, demultiplexer_11_out0, demultiplexer_12_out0, demultiplexer_12_out1,
       demultiplexer_13_out0, demultiplexer_13_out1, demultiplexer_14_out0, demultiplexer_14_out1,
       demultiplexer_15_out0, demultiplexer_17_out1, demultiplexer_18_out0, demultiplexer_18_out1,
       demultiplexer_20_out0, demultiplexer_20_out1, IDLE_q, J, JR, L_A_0, L_TR_0, L_TR_2, L_TR_4, L_TR_5,
       L_TR_6, LHALT0, LOAD_q, LOAD_RAM_2_q, LOAD_RAM_3_q, LOAD_RAM_q, LPC0, LPC2, LRAM1, MFHI, MFLO, OPT0,
       OPT1, OPT2, OPT3, or_1_out, or_2_out, or_4_out, or_5_out, or_7_out, or_9_out, or_13_out, or_14_out,
       or_17_out, or_24_out, or_26_out, or_27_out, REG00, REG01, REG02, REG03, REG10, REG11, REG14, REG20,
       REGW0, REGW4, RST_R_0, RST_R_1, RST_R_2, RST_W_0, RST_W_1, TO_IDLE, TR_1_0, TR_1_5, WAIT_FOR_ALU_q,
       WE0, WE1, WE2, WE4, WE5, WE6, WE7, WHILE_END, While_q;

  Demultiplexer #(.select(3), .enable("false")) demultiplexer_1 (
    .out0(demultiplexer_1_out0), .out1(demultiplexer_1_out1), .out2(demultiplexer_1_out2),
    .out3(demultiplexer_1_out3), .out4(demultiplexer_1_out4), .out5(demultiplexer_1_out5),
    .out6(demultiplexer_1_out6), .out7(demultiplexer_1_out7), .in(OPT0), .sel(in_8));
  Demultiplexer #(.select(3), .enable("false")) demultiplexer_2 (
    .out0(BEQ), .out1(BNE), .out2(BLEZ), .out3(BGTZ), .out4(BLTZ), .out5(J), .out6(JR), .in(OPT2), .sel(in_8));  // open: out7
  D_Flip_Flop #(.trigger("falling")) Halt (.clk(in_1), .D(TO_IDLE), .Q(LHALT0), .reset(in_3));  // open: Qn, preset, en
  D_Flip_Flop #(.trigger("falling")) WAIT_FOR_ALU (
    .clk(in_1), .D(or_1_out), .Q(WAIT_FOR_ALU_q), .reset(in_3));  // open: Qn, preset, en
  or or_1 (or_1_out, demultiplexer_3_out0, out_38);
  not not_1 (A1____A2, in_2);
  or or_2 (or_2_out, demultiplexer_1_out0, demultiplexer_1_out1);
  or or_3 (out_38, demultiplexer_1_out2, demultiplexer_1_out3);
  or or_4 (or_4_out, demultiplexer_1_out4, demultiplexer_1_out5, demultiplexer_1_out6, demultiplexer_1_out7);
  Demultiplexer #(.enable("false")) demultiplexer_3 (
    .out0(demultiplexer_3_out0), .out1(out_37), .in(WAIT_FOR_ALU_q), .sel(in_14));
  D_Flip_Flop #(.trigger("falling")) IDLE (.clk(in_1), .D(or_5_out), .Q(IDLE_q), .preset(in_3));  // open: Qn, en, reset
  or or_5 (or_5_out, demultiplexer_4_out0, LHALT0);
  or or_6 (REGW0, or_2_out, or_4_out);
  Demultiplexer #(.enable("false")) demultiplexer_4 (
    .out0(demultiplexer_4_out0), .out1(demultiplexer_4_out1), .in(IDLE_q), .sel(in_3));
  D_Flip_Flop #(.trigger("falling")) PC____4 (
    .clk(in_1), .D(WHILE_END), .Q(LPC0), .reset(in_3));  // open: Qn, preset, en
  or or_7 (or_7_out, REGW0, REG00);
  or or_8 (WE0, or_7_out, out_37);
  Demultiplexer #(.enable("false")) demultiplexer_5 (.out0(demultiplexer_5_out0), .out1(BRANCH0), .in(BEQ), .sel(in_2));
  Demultiplexer #(.enable("false")) demultiplexer_6 (
    .out0(demultiplexer_6_out0), .out1(BRANCH1), .in(BNE), .sel(A1____A2));
  Demultiplexer #(.enable("false")) demultiplexer_7 (
    .out0(demultiplexer_7_out0), .out1(BRANCH2), .in(BGTZ), .sel(in_5));
  or or_9 (or_9_out, demultiplexer_4_out1, LPC0);
  D_Flip_Flop #(.trigger("falling")) While (.clk(in_1), .D(or_9_out), .Q(While_q));  // open: Qn, preset, en, reset
  Demultiplexer #(.enable("false")) demultiplexer_8 (.out0(L_A_0), .out1(TO_IDLE), .in(While_q), .sel(in_13));
  or or_10 (WE6, demultiplexer_7_out0, demultiplexer_6_out0, demultiplexer_5_out0, demultiplexer_10_out0, demultiplexer_11_out0);
  Demultiplexer #(.select(3), .enable("false")) demultiplexer_9 (
    .out0(REG00), .out1(L_TR_2), .out2(out_28), .out3(ADR10), .out4(LRAM1), .out5(MFHI), .out6(MFLO),
    .in(OPT1), .sel(in_8));  // open: out7
  or or_11 (BRANCH, BRANCH0, BRANCH3, BRANCH1, BRANCH2, BRANCH4);
  D_Flip_Flop #(.trigger("falling")) u_BRANCH (.clk(in_1), .D(BRANCH), .Q(WE4), .reset(in_3));  // open: Qn, preset, en
  Demultiplexer #(.enable("false")) demultiplexer_10 (
    .out0(demultiplexer_10_out0), .out1(BRANCH3), .in(BLEZ), .sel(in_7));
  Demultiplexer #(.enable("false")) demultiplexer_11 (
    .out0(demultiplexer_11_out0), .out1(BRANCH4), .in(BLTZ), .sel(in_9));
  D_Flip_Flop #(.trigger("falling")) Set_ADDR (
    .clk(in_1), .D(L_A_0), .Q(RST_R_0), .reset(in_3));  // open: Qn, preset, en
  or or_12 (out_18[0], L_TR_2, out_28);
  D_Flip_Flop #(.trigger("falling")) LOAD_RAM (
    .clk(in_1), .D(or_13_out), .Q(LOAD_RAM_q), .reset(in_3));  // open: Qn, preset, en
  or or_13 (or_13_out, demultiplexer_12_out0, RST_R_0);
  Demultiplexer #(.enable("false")) demultiplexer_12 (
    .out0(demultiplexer_12_out0), .out1(demultiplexer_12_out1), .in(LOAD_RAM_q), .sel(in_4));
  or or_14 (or_14_out, demultiplexer_13_out0, RST_R_2);
  D_Flip_Flop #(.trigger("falling")) SET_ADDR_2 (
    .clk(in_1), .D(L_TR_2), .Q(RST_R_2), .reset(in_3));  // open: Qn, preset, en
  D_Flip_Flop #(.trigger("falling")) SET_ADDR_3 (
    .clk(in_1), .D(out_28), .Q(RST_W_1), .reset(in_3));  // open: Qn, preset, en
  or or_15 (LPC2, J, JR);
  or or_16 (CS0, LOAD_RAM_q, out_15);
  D_Flip_Flop #(.trigger("falling")) LOAD_RAM_2 (
    .clk(in_1), .D(or_14_out), .Q(LOAD_RAM_2_q), .reset(in_3));  // open: Qn, preset, en
  or or_17 (or_17_out, RST_W_1, demultiplexer_14_out0);
  D_Flip_Flop #(.trigger("falling")) JUMP (.clk(in_1), .D(LPC2), .Q(WE5), .reset(in_3));  // open: Qn, preset, en
  D_Flip_Flop #(.trigger("falling")) CHANGE_TR (
    .clk(in_1), .D(demultiplexer_12_out1), .Q(out_15), .reset(in_3));  // open: Qn, preset, en
  or or_18 (CS4, LOAD_RAM_2_q, REG10);
  Demultiplexer #(.enable("false")) demultiplexer_13 (
    .out0(demultiplexer_13_out0), .out1(demultiplexer_13_out1), .in(LOAD_RAM_2_q), .sel(in_4));
  D_Flip_Flop #(.trigger("falling")) WRITE_RAM (
    .clk(in_1), .D(or_17_out), .Q(CS3), .reset(in_3));  // open: Qn, preset, en
  D_Flip_Flop #(.trigger("falling")) CHANGE_TR_2 (
    .clk(in_1), .D(out_15), .Q(out_16[0]), .reset(in_3));  // open: Qn, preset, en
  D_Flip_Flop #(.trigger("falling")) WRITE_REG (
    .clk(in_1), .D(demultiplexer_13_out1), .Q(REG10), .reset(in_3));  // open: Qn, preset, en
  Demultiplexer #(.enable("false")) demultiplexer_14 (
    .out0(demultiplexer_14_out0), .out1(demultiplexer_14_out1), .in(CS3), .sel(in_6));
  Demultiplexer #(.select(3), .enable("false")) demultiplexer_15 (
    .out0(demultiplexer_15_out0), .out1(out_21), .out2(out_19), .out3(L_TR_5), .out4(L_TR_6), .in(OPT3),
    .sel(in_8));  // open: out5, out6, out7
  D_Flip_Flop #(.trigger("falling")) SET_A1 (
    .clk(in_1), .D(out_16[0]), .Q(out_24), .reset(in_3));  // open: Qn, preset, en
  or or_19 (out_33, RST_R_0, RST_R_1, RST_R_2);
  or or_20 (out_36, RST_W_0, RST_W_1);
  or or_21 (WE2, REG10, demultiplexer_14_out1);
  or or_22 (L_TR_0, out_16[0], CHANGE_TR_3_q, TR_1_0);
  D_Flip_Flop #(.trigger("falling")) CHANGE_TR_3 (
    .clk(in_1), .D(out_24), .Q(CHANGE_TR_3_q), .reset(in_3));  // open: Qn, preset, en
  D_Flip_Flop #(.trigger("falling")) SET_TR (.clk(in_1), .D(L_TR_5), .Q(REG03), .reset(in_3));  // open: Qn, preset, en
  D_Flip_Flop #(.trigger("falling")) SET_A2 (
    .clk(in_1), .D(CHANGE_TR_3_q), .Q(out_27), .reset(in_3));  // open: Qn, preset, en
  D_Flip_Flop #(.trigger("falling")) SET_TR_2 (
    .clk(in_1), .D(L_TR_6), .Q(REG14), .reset(in_3));  // open: Qn, preset, en
  D_Flip_Flop #(.trigger("falling")) CHANGE_TR_4 (
    .clk(in_1), .D(out_27), .Q(TR_1_0), .reset(in_3));  // open: Qn, preset, en
  Demultiplexer #(.enable("false")) demultiplexer_16 (.out0(REG02), .out1(out_23), .in(REG14), .sel(in_11));
  D_Flip_Flop #(.trigger("falling")) SET_A3 (.clk(in_1), .D(TR_1_0), .Q(out_29), .reset(in_3));  // open: Qn, preset, en
  D_Flip_Flop #(.trigger("falling")) SP_W (.clk(in_1), .D(LRAM1), .Q(ADR11), .reset(in_3));  // open: Qn, preset, en
  or or_23 (WE7, demultiplexer_15_out0, out_21, out_19, REG03, REG14);
  D_Flip_Flop #(.trigger("falling")) IF_I (.clk(in_1), .D(out_29), .Q(out_17), .reset(in_3));  // open: Qn, preset, en
  D_Flip_Flop #(.trigger("falling")) SET_ADDR_4 (
    .clk(in_1), .D(ADR10), .Q(RST_R_1), .reset(in_3));  // open: Qn, preset, en
  Demultiplexer #(.enable("false")) demultiplexer_17 (
    .out0(TR_1_5), .out1(demultiplexer_17_out1), .in(out_17), .sel(in_12));
  or or_24 (or_24_out, demultiplexer_18_out0, RST_R_1);
  D_Flip_Flop #(.trigger("falling")) SET_ADDR_5 (
    .clk(in_1), .D(ADR11), .Q(RST_W_0), .reset(in_3));  // open: Qn, preset, en
  or or_25 (L_TR_4, MFHI, MFLO);
  Demultiplexer #(.enable("false")) demultiplexer_18 (
    .out0(demultiplexer_18_out0), .out1(demultiplexer_18_out1), .in(LOAD_RAM_3_q), .sel(in_4));
  D_Flip_Flop #(.trigger("falling")) LOAD_RAM_3 (
    .clk(in_1), .D(or_24_out), .Q(LOAD_RAM_3_q), .reset(in_3));  // open: Qn, preset, en
  or or_26 (or_26_out, RST_W_0, demultiplexer_20_out0);
  D_Flip_Flop #(.trigger("falling")) LOAD (
    .clk(in_1), .D(or_27_out), .Q(LOAD_q), .reset(in_3));  // open: Qn, preset, en
  or or_27 (or_27_out, TR_1_5, demultiplexer_17_out1);
  D_Flip_Flop #(.trigger("falling")) WRITE_RAM_2 (
    .clk(in_1), .D(or_26_out), .Q(CS2), .reset(in_3));  // open: Qn, preset, en
  D_Flip_Flop #(.trigger("falling")) SET_TR_3 (.clk(in_1), .D(MFHI), .Q(REG01), .reset(in_3));  // open: Qn, preset, en
  D_Flip_Flop #(.trigger("falling")) SET_TR_4 (.clk(in_1), .D(MFLO), .Q(REG20), .reset(in_3));  // open: Qn, preset, en
  Demultiplexer #(.select(2), .enable("false")) demultiplexer_19 (
    .out0(OPT0), .out1(OPT1), .out2(OPT2), .out3(OPT3), .in(LOAD_q), .sel(in_10));
  or or_28 (CS1, LOAD_RAM_3_q, REG11);
  D_Flip_Flop #(.trigger("falling")) WRITE_REG_2 (
    .clk(in_1), .D(demultiplexer_18_out1), .Q(REG11), .reset(in_3));  // open: Qn, preset, en
  Demultiplexer #(.enable("false")) demultiplexer_20 (
    .out0(demultiplexer_20_out0), .out1(demultiplexer_20_out1), .in(CS2), .sel(in_6));
  or or_29 (REGW4, REG01, REG20);
  or or_30 (WHILE_END, WE0, WE1, WE7, WE2, REGW4, WE4, WE5, WE6);
  or or_31 (out_40, out_28, LRAM1);
  or or_32 (out_41[0], REG00, REG01, REG02, REG03);
  or or_33 (out_41[1], REG10, REG11, REG01, REG14);
  or or_34 (out_41[2], REG20, REG03, REG14);
  D_Flip_Flop #(.trigger("falling")) SP_W_2 (.clk(in_1), .D(REG11), .Q(out_31), .reset(in_3));  // open: Qn, preset, en
  or or_35 (WE1, out_31, demultiplexer_20_out1);
  or or_36 (out_39, REGW0, REG00, REG10, REG14, REG11, REGW4, REG03);
  or or_37 (out_22, L_A_0, out_18[0], ADR11, ADR10);
  or or_38 (out_25[0], BRANCH, JR);
  or or_39 (out_25[1], J, JR);
  or or_40 (out_32, LHALT0, out_21);
  or or_41 (out_34, LPC0, BRANCH, LPC2);
  or or_42 (out_16[1], TR_1_0, L_TR_4, ADR10, L_TR_5, L_TR_6, TR_1_5);
  or or_43 (out_20, L_TR_0, out_17, L_TR_2, ADR10, L_TR_4, L_TR_5, L_TR_6);
  or or_44 (out_30, CS0, CS1, CS2, CS3, CS4);
  or or_45 (out_35, out_31, LRAM1);
  or or_46 (out_18[1], ADR10, ADR11);
  or or_47 (out_26, CS2, CS3);

  // Other names for the same wires on the sheet: A1___0 = in_9; A1___0_t = in_5; A1____0 = in_7; A1____A2_t = in_2;
  //   ADDR_0 = out_18[0]; ADDR_SEL[1:0] = out_18; L_A_1 = out_18[0]; ADDR_1 = out_18[1]; ALU_DONE = in_14; CLK = in_1;
  //   CLR = in_3; CS = out_30; HALT = in_13; I = in_12; KBD_AVAIL = in_11; KBD_ENABLE = out_23; L_A1 = out_24;
  //   L_A2 = out_27; L_A3 = out_29; L_A_3 = ADR11; L_ADDR = out_22; L_HALT = out_32; L_HiLo = out_37; L_INS = out_15;
  //   L_PC = out_34; L_RAM_IN = out_40; L_TARGET_REG = out_20; L_ALU_IN_B = out_17; L_TR_1 = out_17; HALT_IN = out_21;
  //   LHALT1 = out_21; LW = L_TR_2; OP[2:0] = in_8; OPT[1:0] = in_10; PC_IN_SEL[1:0] = out_25; PCI0 = out_25[0];
  //   PCI1 = out_25[1]; LPC1 = BRANCH; PCI00 = BRANCH; PCI10 = J; PCI01 = JR; PCI11 = JR; RAM_READ = in_4;
  //   RAM_WRITE = in_6; REG12 = REG01; REG0 = out_41[0]; REG_IN_SEL[2:0] = out_41; REG1 = out_41[1]; REG2 = out_41[2];
  //   REG_W = out_39; REGW2 = REG10; REGW3 = REG11; REG21 = REG03; REGW5 = REG03; REG22 = REG14; REGW6 = REG14;
  //   RESET_READ = out_33; RESET_WRITE = out_36; RW = out_26; RW0 = CS2; RW1 = CS3; REGW1 = REG00; SLT = REG00;
  //   SP_W = out_35; SP_plus_plus = out_31; SPW0 = out_31; PUSH = LRAM1; SPW1 = LRAM1; MUL_DIV = out_38;
  //   START_ALU = out_38; LRAM0 = out_28; RAM_IN_SEL = out_28; SW = out_28; TARGET_REG_SEL[1:0] = out_16;
  //   TR_0 = out_16[0]; TR_1 = out_16[1]; L_A_2 = ADR10; L_TR_3 = ADR10; POP = ADR10; TR_1_1 = ADR10; TR_1_2 = L_TR_4;
  //   TR_1_3 = L_TR_5; TR_1_4 = L_TR_6; TTY_ENABLE = out_19; WE3 = REGW4
endmodule

module DATA_PATH (
  input  in_1,
  input  [31:0] CURRENT_BANK,
  input  in_3,
  input  in_4,
  input  CLR,
  input  in_6,
  input  CLK,
  input  in_8,
  input  in_9,
  input  in_10,
  input  [1:0] in_11,
  input  in_12,
  input  in_13,
  input  [1:0] in_14,
  input  in_15,
  input  in_16,
  input  [6:0] in_17,
  input  in_18,
  input  in_19,
  input  in_20,
  input  [1:0] in_21,
  input  in_22,
  input  in_23,
  input  in_24,
  input  [2:0] in_25,
  output out_26,
  output out_27,
  output out_28,
  output out_29,
  output [6:0] out_30,
  output out_31,
  output [2:0] out_32,
  output [31:0] out_33,
  output [1:0] out_34,
  output out_35,
  output [31:0] out_36,
  output out_37
);

  wire and_1_out, and_2_out, and_3_out, and_4_out, and_5_out, and_6_out, and_7_out, and_8_out, and_9_out,
       and_10_out, and_11_out, comparator_2_eq, LS, not_1_out, not_2_out, U;
  wire [4:0] ARG_1, ARG_2, ARG_3, multiplexer_3_out, TARGET_REG;
  wire [13:0] bit_extender_1_out;
  wire [15:0] CONST;
  wire [25:0] JUMP_D;
  wire [31:0] A2, A3, adder_1_out, adder_2_out, adder_3_out, adder_4_out, ALU_IN_B, ALU_OUT, ALU_OUT_2,
       bit_extender_2_out, bit_extender_3_out, bit_extender_4_out, bit_extender_5_out, Hi, INS, Lo,
       multiplexer_1_out, multiplexer_2_out, multiplexer_4_out, multiplexer_5_out, multiplexer_6_out, PC,
       random_1_out, REG_IN, REG_OUT, SP, SP_IN, subtractor_1_out, subtractor_2_out, subtractor_3_out;
  wire [31:7] A1;

  Register #(.width(32)) u_INS (.D(CURRENT_BANK), .Q(INS), .clk(and_1_out), .clr(CLR));  // open: en
  and and_1 (and_1_out, in_1, CLK);
  assign bit_extender_1_out = {{13{CONST[15]}}, CONST[15]};  // Bit_Extender bit_extender_1
  assign bit_extender_2_out = {{16{CONST[15]}}, CONST};  // Bit_Extender bit_extender_2
  Multiplexer #(.width(32), .enable("false")) multiplexer_1 (
    .in0(A2), .in1(bit_extender_2_out), .out(multiplexer_1_out), .sel(out_35));
  Adder #(.width(32)) adder_1 (.a({bit_extender_1_out, CONST, 2'b00}), .b(PC), .out(adder_1_out));  // open: cin, cout
  Adder #(.width(32)) adder_2 (.a(PC), .b(32'h4), .out(adder_2_out));  // open: cin, cout
  Register #(.width(1)) HALT (.D(in_18), .Q(out_31), .clk(and_2_out), .clr(CLR));  // open: en
  and and_2 (and_2_out, in_15, CLK);
  Register #(.width(32)) u_ALU_IN_B (.D(multiplexer_1_out), .Q(ALU_IN_B), .clk(and_3_out), .clr(CLR));  // open: en
  and and_3 (and_3_out, in_3, CLK);
  Multiplexer #(.select(2), .width(32), .enable("false")) multiplexer_2 (
    .in0(adder_2_out), .in1(adder_1_out), .in2(subtractor_1_out), .in3(subtractor_2_out),
    .out(multiplexer_2_out), .sel(in_21));
  and and_4 (and_4_out, in_16, CLK);
  Register #(.width(32)) u_PC (.D(multiplexer_2_out), .Q(PC), .clk(and_4_out), .clr(CLR));  // open: en
  Multiplexer #(.select(2), .width(5), .enable("false")) multiplexer_3 (
    .in0(ARG_2), .in1(ARG_1), .in2(ARG_3), .out(multiplexer_3_out), .sel(in_11));  // open: in3
  Register #(.width(5)) u_TARGET_REG (.D(multiplexer_3_out), .Q(TARGET_REG), .clk(and_5_out), .clr(CLR));  // open: en
  and and_5 (and_5_out, in_4, CLK);
  Subtractor #(.width(32)) subtractor_1 (
    .a({PC[31:28], JUMP_D, 2'b00}), .b(32'h4), .out(subtractor_1_out));  // open: bin, bout
  Subtractor #(.width(32)) subtractor_2 (.a({A1, out_30}), .b(32'h4), .out(subtractor_2_out));  // open: bin, bout
  assign bit_extender_3_out = {{16{CONST[15]}}, CONST};  // Bit_Extender bit_extender_3
  Register #(.width(32)) u_Hi (.D(ALU_OUT_2), .Q(Hi), .clk(and_6_out), .clr(CLR));  // open: en
  and and_6 (and_6_out, in_19, CLK);
  Adder #(.width(32)) adder_3 (.a({A1, out_30}), .b(bit_extender_3_out), .out(adder_3_out));  // open: cin, cout
  Multiplexer #(.select(2), .width(32), .enable("false")) multiplexer_4 (
    .in0(PC), .in1(adder_3_out), .in2(SP), .out(multiplexer_4_out), .sel(in_14));  // open: in3
  and and_7 (and_7_out, in_6, CLK);
  Register #(.width(32)) ADDR (.D(multiplexer_4_out), .Q(out_33), .clk(and_7_out), .clr(CLR));  // open: en
  Multiplexer #(.width(32), .enable("false")) multiplexer_5 (
    .in0({A1, out_30}), .in1(A2), .out(multiplexer_5_out), .sel(in_24));
  Register #(.width(32)) u_Lo (.D(ALU_OUT), .Q(Lo), .clk(and_6_out), .clr(CLR));  // open: en
  Register #(.width(32)) u_A1 (.D(REG_OUT), .Q({A1, out_30}), .clk(and_8_out), .clr(CLR));  // open: en
  and and_8 (and_8_out, in_8, CLK);
  Register #(.width(32)) RAM_IN (.D(multiplexer_5_out), .Q(out_36), .clk(and_9_out), .clr(CLR));  // open: en
  and and_9 (and_9_out, in_22, CLK);
  Comparator #(.width(32)) comparator_1 (.a({A1, out_30}), .b(A2), .eq(out_26));  // open: gt, lt
  Comparator #(.width(32)) comparator_2 (
    .a({A1, out_30}), .b({32{1'b0}}), .gt(out_27), .eq(comparator_2_eq), .lt(out_29));
  and and_10 (and_10_out, in_9, CLK);
  or or_1 (out_28, out_29, comparator_2_eq);
  Register #(.width(32)) u_A2 (.D(REG_OUT), .Q(A2), .clk(and_10_out), .clr(CLR));  // open: en
  Adder #(.width(32)) adder_4 (.a(SP), .b(32'h4), .out(adder_4_out));  // open: cin, cout
  Subtractor #(.width(32)) subtractor_3 (.a(SP), .b(32'h4), .out(subtractor_3_out));  // open: bin, bout
  Register #(.width(32)) u_A3 (.D(REG_OUT), .Q(A3), .clk(and_11_out), .clr(CLR));  // open: en
  and and_11 (and_11_out, in_12, CLK);
  Multiplexer #(.width(32), .enable("false")) multiplexer_6 (
    .in0(subtractor_3_out), .in1(adder_4_out), .out(multiplexer_6_out), .sel(in_10));
  Multiplexer #(.width(32), .enable("false")) multiplexer_7 (
    .in0(SP), .in1(multiplexer_6_out), .out(SP_IN), .sel(in_13));
  ID id_1 (
    .INSTRUCTION(INS), .OP(out_32), .OP_TYPE(out_34), .I(out_35), .U(U), .out_7(ARG_1), .out_8(ARG_2),
    .out_9(ARG_3), .out_10(JUMP_D), .out_11(CONST), .EN(not_1_out));
  not not_1 (not_1_out, CLR);
  not not_2 (not_2_out, CLR);
  Random #(.width(32), .seed(2)) random_1 (.clk(CLK), .out(random_1_out));  // open: next, clr
  assign bit_extender_4_out = {{31{1'b0}}, LS};  // Bit_Extender bit_extender_4
  RF rf_1 (
    .WRITE(in_20), .IN(REG_IN), .SEL(TARGET_REG), .OUT(REG_OUT), .CLK(CLK), .RST(CLR), .SP_IN(SP_IN),
    .SP_OUT(SP));
  ALU alu_1 (
    .IN_A({A1, out_30}), .IN_B(ALU_IN_B), .U(U), .SEL(out_32), .OUT1(ALU_OUT), .OUT2(ALU_OUT_2),
    .START(in_23), .out_10(out_37), .CLK(CLK), .out_9(LS));
  assign bit_extender_5_out = {{25{1'b0}}, in_17};  // Bit_Extender bit_extender_5
  Multiplexer #(.select(3), .width(32), .enable("false")) multiplexer_8 (
    .in0(ALU_OUT), .in1(bit_extender_4_out), .in2(CURRENT_BANK), .in3(Hi), .in4(Lo), .in5(random_1_out),
    .in6(bit_extender_5_out), .in7({32{1'b1}}), .out(REG_IN), .sel(in_25));

  // Other names for the same wires on the sheet: A1___0 = out_29; A1___0_t = out_27; A1____0 = out_28;
  //   A1____A2 = out_26; ADDR[31:0] = out_33; ADDR_SEL[1:0] = in_14; ALU_DONE = out_37; A1[6:0] = out_30;
  //   ALU_IN_A[31:0] = {A1, out_30}; HALT = out_31; HALT_IN = in_18; I = out_35; KBD_DATA[6:0] = in_17; L_A1 = in_8;
  //   L_A2 = in_9; L_A3 = in_12; L_ADDR = in_6; L_ALU_IN_B = in_3; L_HALT = in_15; L_HiLo = in_19; L_INS = in_1;
  //   L_PC = in_16; L_RAM_IN = in_22; L_TARGET_REG = in_4; OP[2:0] = out_32; OPT[1:0] = out_34;
  //   PC_IN_SEL[1:0] = in_21; RAM_IN[31:0] = out_36; RAM_IN_SEL = in_24; REG_IN_SEL[2:0] = in_25; REG_W = in_20;
  //   SP_plus_plus = in_10; SP_W = in_13; START_ALU = in_23; TARGET_REG_SEL[1:0] = in_11

  // Notes on the sheet:
  //   INSTRUCTION DECODER
  //   REGISTRY FETCH
  //   ALU
endmodule

module ADD_64 (
  input  [31:0] IN_A_Lo,
  input  [31:0] IN_A_Hi,
  input  [31:0] IN_B_Lo,
  input  [31:0] IN_B_Hi,
  output [31:0] OUT_Lo,
  output [31:0] OUT_Hi
);

  wire adder_1_cout;

  Adder #(.width(32)) adder_1 (.a(IN_A_Lo), .b(IN_B_Lo), .out(OUT_Lo), .cout(adder_1_cout));  // open: cin
  Adder #(.width(32)) adder_2 (.a(IN_A_Hi), .b(IN_B_Hi), .out(OUT_Hi), .cin(adder_1_cout));  // open: cout
endmodule

module ISOL (
  input  [31:0] IN_A,
  input  [4:0] SEL,
  output [31:0] OUT
);

  wire bitselector_1_out;

  Demultiplexer #(.select(5), .enable("false")) demultiplexer_1 (
    .out0(OUT[0]), .out1(OUT[1]), .out2(OUT[2]), .out3(OUT[3]), .out4(OUT[4]), .out5(OUT[5]), .out6(OUT[6]),
    .out7(OUT[7]), .out8(OUT[8]), .out9(OUT[9]), .out10(OUT[10]), .out11(OUT[11]), .out12(OUT[12]),
    .out13(OUT[13]), .out14(OUT[14]), .out15(OUT[15]), .out16(OUT[16]), .out17(OUT[17]), .out18(OUT[18]),
    .out19(OUT[19]), .out20(OUT[20]), .out21(OUT[21]), .out22(OUT[22]), .out23(OUT[23]), .out24(OUT[24]),
    .out25(OUT[25]), .out26(OUT[26]), .out27(OUT[27]), .out28(OUT[28]), .out29(OUT[29]), .out30(OUT[30]),
    .out31(OUT[31]), .in(bitselector_1_out), .sel(SEL));
  BitSelector #(.width(32)) bitselector_1 (.in(IN_A), .out(bitselector_1_out), .sel(SEL));
endmodule

module PART_UMUL (
  input  [31:0] in_1,
  input  [31:0] in_2,
  input  [31:0] in_3,
  input  [31:0] in_4,
  output [31:0] Transfer,
  output [31:0] OUT_Lo,
  output [31:0] OUT_Hi,
  output ZF,
  output [31:0] SELECTED
);

  wire bitfinder_1_found, comparator_1_eq, or_1_out;
  wire [4:0] INDEX, minus_INDEX;
  wire [31:0] Hi, Lo, shifter_1_out, shifter_2_out;

  BitFinder #(.width(32)) bitfinder_1 (.in(in_2), .index(INDEX), .found(bitfinder_1_found));
  not not_1 (ZF, bitfinder_1_found);
  Subtractor #(.width(5)) subtractor_1 (.a({5{1'b0}}), .b(INDEX), .out(minus_INDEX));  // open: bin, bout
  Shifter #(.width(32)) shifter_1 (.in(in_1), .\dist (INDEX), .out(shifter_1_out));
  Shifter #(.width(32), .shift("lr")) shifter_2 (.in(in_1), .\dist (minus_INDEX), .out(shifter_2_out));
  Multiplexer #(.width(32), .enable("false")) multiplexer_1 (.in0(shifter_1_out), .in1({32{1'b0}}), .out(Lo), .sel(ZF));
  Multiplexer #(.width(32), .enable("false")) multiplexer_2 (
    .in0(shifter_2_out), .in1({32{1'b0}}), .out(Hi), .sel(or_1_out));
  or or_1 (or_1_out, comparator_1_eq, ZF);
  Comparator #(.width(5)) comparator_1 (.a(INDEX), .b({5{1'b0}}), .eq(comparator_1_eq));  // open: gt, lt
  ADD_64 add_64_1 (.IN_A_Lo(Lo), .IN_A_Hi(Hi), .IN_B_Lo(in_3), .IN_B_Hi(in_4), .OUT_Lo(OUT_Lo), .OUT_Hi(OUT_Hi));
  ISOL isol_1 (.IN_A(in_2), .SEL(INDEX), .OUT(SELECTED));

  assign Transfer = in_1;

  // Other names for the same wires on the sheet: C_Hi[31:0] = in_4; C_Lo[31:0] = in_3; IN[31:0] = in_1;
  //   PARTIAL[31:0] = in_2; ZERO = ZF
endmodule

module UMUL_A (
  input  [31:0] IN_A,
  input  [31:0] IN_B,
  input  START,
  input  CLK,
  output [31:0] OUT_Lo,
  output [31:0] OUT_Hi,
  output out_7
);

  wire and_1_out, and_2_out, and_3_out, and_4_out, CONTINUE, demultiplexer_1_out0, demultiplexer_1_out1,
       demultiplexer_2_out0, demultiplexer_2_out1, IDLE_q, L_Hi, L_PARTIAL, L_SELECTED, LP0, or_1_out,
       or_2_out, ZF;
  wire [31:0] multiplexer_1_out, N_Carry_Hi, N_Carry_Lo, N_SELECTED, PARTIAL, SELECTED, subtractor_1_out;

  or or_1 (or_1_out, demultiplexer_1_out0, out_7);
  Subtractor #(.width(32)) subtractor_1 (.a(PARTIAL), .b(SELECTED), .out(subtractor_1_out));  // open: bin, bout
  Multiplexer #(.width(32), .enable("false")) multiplexer_1 (
    .in0(IN_B), .in1(subtractor_1_out), .out(multiplexer_1_out), .sel(CONTINUE));
  and and_1 (and_1_out, CLK, L_PARTIAL);
  Demultiplexer #(.enable("false")) demultiplexer_1 (
    .out0(demultiplexer_1_out0), .out1(demultiplexer_1_out1), .in(IDLE_q), .sel(START));
  D_Flip_Flop #(.trigger("falling")) IDLE (.clk(CLK), .D(or_1_out), .Q(IDLE_q), .preset(START));  // open: Qn, en, reset
  Register #(.width(32)) u_PARTIAL (.D(multiplexer_1_out), .Q(PARTIAL), .clk(and_1_out), .clr(START));  // open: en
  PART_UMUL part_umul_1 (
    .in_1(IN_A), .in_2(PARTIAL), .in_3(OUT_Lo), .in_4(OUT_Hi), .OUT_Lo(N_Carry_Lo), .OUT_Hi(N_Carry_Hi),
    .ZF(ZF), .SELECTED(N_SELECTED));  // open: Transfer
  Register #(.width(32)) Carry_Lo (.D(N_Carry_Lo), .Q(OUT_Lo), .clk(and_2_out), .clr(START));  // open: en
  and and_2 (and_2_out, CLK, L_Hi);
  D_Flip_Flop #(.trigger("falling")) DO (.clk(CLK), .D(demultiplexer_1_out1), .Q(LP0));  // open: Qn, preset, en, reset
  or or_2 (or_2_out, LP0, CONTINUE);
  Register #(.width(32)) Carry_Hi (.D(N_Carry_Hi), .Q(OUT_Hi), .clk(and_3_out), .clr(START));  // open: en
  and and_3 (and_3_out, CLK, L_Hi);
  D_Flip_Flop #(.trigger("falling")) DO_2 (
    .clk(CLK), .D(or_2_out), .Q(L_SELECTED), .reset(START));  // open: Qn, preset, en
  or or_3 (L_PARTIAL, LP0, CONTINUE);
  Register #(.width(32)) u_SELECTED (.D(N_SELECTED), .Q(SELECTED), .clk(and_4_out), .clr(START));  // open: en
  and and_4 (and_4_out, CLK, L_SELECTED);
  D_Flip_Flop #(.trigger("falling")) SET_SELECTED (
    .clk(CLK), .D(L_SELECTED), .Q(L_Hi), .reset(START));  // open: Qn, preset, en
  Demultiplexer #(.enable("false")) demultiplexer_2 (
    .out0(demultiplexer_2_out0), .out1(demultiplexer_2_out1), .in(L_Hi), .sel(ZF));
  D_Flip_Flop #(.trigger("falling")) SET_PAR (
    .clk(CLK), .D(demultiplexer_2_out0), .Q(CONTINUE), .reset(START));  // open: Qn, preset, en
  D_Flip_Flop #(.trigger("falling")) SET_LOHI (
    .clk(CLK), .D(demultiplexer_2_out1), .Q(out_7), .reset(START));  // open: Qn, preset, en

  // Other names for the same wires on the sheet: Carry_Hi[31:0] = OUT_Hi; Carry_Lo[31:0] = OUT_Lo; CLR = START;
  //   L_Lo = L_Hi; LP1 = CONTINUE; PARTIAL_SEL = CONTINUE; DONE = out_7; TO_IDLE = out_7
endmodule
